// Logisim project trabalho.circ as structural Verilog: 4 circuits, main circuit main
module main (
);

  wire clock_1_out;
  wire [11:0] adder_1_out, register_1_q, rom_1_data;

  Clock clock_1 (.out(clock_1_out));
  Register #(.width(12)) register_1 (.D(adder_1_out), .clk(clock_1_out), .Q(register_1_q));  // open: en, clr
  Adder #(.width(12)) adder_1 (.a(register_1_q), .b(12'h1), .out(adder_1_out));  // open: cin, cout
  ROM #(.addrWidth(12), .dataWidth(12)) rom_1 (.addr(register_1_q), .data(rom_1_data));
endmodule

module regs (
  input  [11:0] D,
  input  wr1,
  input  wr2,
  input  wr3,
  input  wr4,
  input  wr5,
  input  wr6,
  input  wr7,
  input  wr8,
  input  wr9,
  input  wr10,
  input  wr11,
  input  wr12,
  input  wr13,
  input  wr14,
  input  wr15,
  input  wr16,
  output [11:0] sr1,
  output [11:0] sr2,
  output [11:0] sr3,
  output [11:0] sr4,
  output [11:0] sr5,
  output [11:0] sr6,
  output [11:0] sr7,
  output [11:0] sr8,
  output [11:0] sr9,
  output [11:0] sr10,
  output [11:0] sr11,
  output [11:0] sr12,
  output [11:0] sr13,
  output [11:0] sr14,
  output [11:0] sr15,
  output [11:0] sr16
);

  wire clk;
  wire [11:0] multiplexer_1_out, multiplexer_2_out, multiplexer_3_out, multiplexer_4_out, multiplexer_5_out,
       multiplexer_6_out, multiplexer_7_out, multiplexer_8_out, multiplexer_9_out, multiplexer_10_out,
       multiplexer_11_out, multiplexer_12_out, multiplexer_13_out, multiplexer_14_out, multiplexer_15_out,
       multiplexer_16_out;

  Clock clock_1 (.out(clk));
  Multiplexer #(.width(12)) multiplexer_1 (.in0(sr1), .in1(D), .out(multiplexer_1_out), .sel(wr1));
  Multiplexer #(.width(12)) multiplexer_2 (.in0(sr2), .in1(D), .out(multiplexer_2_out), .sel(wr2));
  Multiplexer #(.width(12)) multiplexer_3 (.in0(sr3), .in1(D), .out(multiplexer_3_out), .sel(wr3));
  Multiplexer #(.width(12)) multiplexer_4 (.in0(sr4), .in1(D), .out(multiplexer_4_out), .sel(wr4));
  Multiplexer #(.width(12)) multiplexer_5 (.in0(sr5), .in1(D), .out(multiplexer_5_out), .sel(wr5));
  Multiplexer #(.width(12)) multiplexer_6 (.in0(sr6), .in1(D), .out(multiplexer_6_out), .sel(wr6));
  Multiplexer #(.width(12)) multiplexer_7 (.in0(sr7), .in1(D), .out(multiplexer_7_out), .sel(wr7));
  Multiplexer #(.width(12)) multiplexer_8 (.in0(sr8), .in1(D), .out(multiplexer_8_out), .sel(wr8));
  Multiplexer #(.width(12)) multiplexer_9 (.in0(sr9), .in1(D), .out(multiplexer_9_out), .sel(wr9));
  Multiplexer #(.width(12)) multiplexer_10 (.in0(sr10), .in1(D), .out(multiplexer_10_out), .sel(wr10));
  Multiplexer #(.width(12)) multiplexer_11 (.in0(sr11), .in1(D), .out(multiplexer_11_out), .sel(wr11));
  Multiplexer #(.width(12)) multiplexer_12 (.in0(sr12), .in1(D), .out(multiplexer_12_out), .sel(wr12));
  Multiplexer #(.width(12)) multiplexer_13 (.in0(sr13), .in1(D), .out(multiplexer_13_out), .sel(wr13));
  Multiplexer #(.width(12)) multiplexer_14 (.in0(sr14), .in1(D), .out(multiplexer_14_out), .sel(wr14));
  Multiplexer #(.width(12)) multiplexer_15 (.in0(sr15), .in1(D), .out(multiplexer_15_out), .sel(wr15));
  Multiplexer #(.width(12)) multiplexer_16 (.in0(sr16), .in1(D), .out(multiplexer_16_out), .sel(wr16));
  Register #(.width(12)) reg1 (.D(multiplexer_1_out), .clk(clk), .Q(sr1));  // open: en, clr
  Register #(.width(12)) reg2 (.D(multiplexer_2_out), .clk(clk), .Q(sr2));  // open: en, clr
  Register #(.width(12)) reg3 (.D(multiplexer_3_out), .clk(clk), .Q(sr3));  // open: en, clr
  Register #(.width(12)) reg4 (.D(multiplexer_4_out), .clk(clk), .Q(sr4));  // open: en, clr
  Register #(.width(12)) reg5 (.D(multiplexer_5_out), .clk(clk), .Q(sr5));  // open: en, clr
  Register #(.width(12)) reg6 (.D(multiplexer_6_out), .clk(clk), .Q(sr6));  // open: en, clr
  Register #(.width(12)) reg7 (.D(multiplexer_7_out), .clk(clk), .Q(sr7));  // open: en, clr
  Register #(.width(12)) reg8 (.D(multiplexer_8_out), .clk(clk), .Q(sr8));  // open: en, clr
  Register #(.width(12)) reg9 (.D(multiplexer_9_out), .clk(clk), .Q(sr9));  // open: en, clr
  Register #(.width(12)) reg10 (.D(multiplexer_10_out), .clk(clk), .Q(sr10));  // open: en, clr
  Register #(.width(12)) reg11 (.D(multiplexer_11_out), .clk(clk), .Q(sr11));  // open: en, clr
  Register #(.width(12)) reg12 (.D(multiplexer_12_out), .clk(clk), .Q(sr12));  // open: en, clr
  Register #(.width(12)) reg13 (.D(multiplexer_13_out), .clk(clk), .Q(sr13));  // open: en, clr
  Register #(.width(12)) reg14 (.D(multiplexer_14_out), .clk(clk), .Q(sr14));  // open: en, clr
  Register #(.width(12)) reg15 (.D(multiplexer_15_out), .clk(clk), .Q(sr15));  // open: en, clr
  Register #(.width(12)) reg16 (.D(multiplexer_16_out), .clk(clk), .Q(sr16));  // open: en, clr

  // Other names for the same wires on the sheet: dado[11:0] = D
endmodule

module breg (
  input  [11:0] D,
  input  W,
  input  [3:0] rd,
  input  [3:0] rs1,
  input  [3:0] rs2,
  output [11:0] sr1,
  output [11:0] sr2
);

  wire demultiplexer_1_out0, demultiplexer_1_out1, demultiplexer_1_out2, demultiplexer_1_out3,
       demultiplexer_1_out4, demultiplexer_1_out5, demultiplexer_1_out6, demultiplexer_1_out7,
       demultiplexer_1_out8, demultiplexer_1_out9, demultiplexer_1_out10, demultiplexer_1_out11,
       demultiplexer_1_out12, demultiplexer_1_out13, demultiplexer_1_out14, demultiplexer_1_out15;
  wire [11:0] regs_1_sr1, regs_1_sr2, regs_1_sr3, regs_1_sr4, regs_1_sr5, regs_1_sr6, regs_1_sr7, regs_1_sr8,
       regs_1_sr9, regs_1_sr10, regs_1_sr11, regs_1_sr12, regs_1_sr13, regs_1_sr14, regs_1_sr15, regs_1_sr16;

  Demultiplexer #(.select(4)) demultiplexer_1 (
    .out0(demultiplexer_1_out0), .out1(demultiplexer_1_out1), .out2(demultiplexer_1_out2),
    .out3(demultiplexer_1_out3), .out4(demultiplexer_1_out4), .out5(demultiplexer_1_out5),
    .out6(demultiplexer_1_out6), .out7(demultiplexer_1_out7), .out8(demultiplexer_1_out8),
    .out9(demultiplexer_1_out9), .out10(demultiplexer_1_out10), .out11(demultiplexer_1_out11),
    .out12(demultiplexer_1_out12), .out13(demultiplexer_1_out13), .out14(demultiplexer_1_out14),
    .out15(demultiplexer_1_out15), .in(W), .sel(rd));
  regs regs_1 (
    .D(D), .wr1(demultiplexer_1_out0), .wr2(demultiplexer_1_out1), .wr3(demultiplexer_1_out2),
    .wr4(demultiplexer_1_out3), .wr5(demultiplexer_1_out4), .wr6(demultiplexer_1_out5),
    .wr7(demultiplexer_1_out6), .wr8(demultiplexer_1_out7), .wr9(demultiplexer_1_out8),
    .wr10(demultiplexer_1_out9), .wr11(demultiplexer_1_out10), .wr12(demultiplexer_1_out11),
    .wr13(demultiplexer_1_out12), .wr14(demultiplexer_1_out13), .wr15(demultiplexer_1_out14),
    .wr16(demultiplexer_1_out15), .sr1(regs_1_sr1), .sr2(regs_1_sr2), .sr3(regs_1_sr3), .sr4(regs_1_sr4),
    .sr5(regs_1_sr5), .sr6(regs_1_sr6), .sr7(regs_1_sr7), .sr8(regs_1_sr8), .sr9(regs_1_sr9),
    .sr10(regs_1_sr10), .sr11(regs_1_sr11), .sr12(regs_1_sr12), .sr13(regs_1_sr13), .sr14(regs_1_sr14),
    .sr15(regs_1_sr15), .sr16(regs_1_sr16));
  Multiplexer #(.select(4), .width(12)) multiplexer_1 (
    .in0(regs_1_sr1), .in1(regs_1_sr2), .in2(regs_1_sr3), .in3(regs_1_sr4), .in4(regs_1_sr5),
    .in5(regs_1_sr6), .in6(regs_1_sr7), .in7(regs_1_sr8), .in8(regs_1_sr9), .in9(regs_1_sr10),
    .in10(regs_1_sr11), .in11(regs_1_sr12), .in12(regs_1_sr13), .in13(regs_1_sr14), .in14(regs_1_sr15),
    .in15(regs_1_sr16), .out(sr1), .sel(rs1));
  Multiplexer #(.select(4), .width(12)) multiplexer_2 (
    .in0(regs_1_sr1), .in1(regs_1_sr2), .in2(regs_1_sr3), .in3(regs_1_sr4), .in4(regs_1_sr5),
    .in5(regs_1_sr6), .in6(regs_1_sr7), .in7(regs_1_sr8), .in8(regs_1_sr9), .in9(regs_1_sr10),
    .in10(regs_1_sr11), .in11(regs_1_sr12), .in12(regs_1_sr13), .in13(regs_1_sr14), .in14(regs_1_sr15),
    .in15(regs_1_sr16), .out(sr2), .sel(rs2));
endmodule

module ULA (
  input  [11:0] r1,
  input  [11:0] r2,
  input  [2:0] op,
  output [11:0] O
);

  wire [11:0] adder_1_out, and_1_out, not_1_out, or_1_out, subtractor_1_out, xor_1_out;

  assign and_1_out = r1 & r2;  // AND_Gate and_1, 12 bits wide
  assign or_1_out = r1 | r2;  // OR_Gate or_1, 12 bits wide
  assign xor_1_out = r1 ^ r2;  // XOR_Gate xor_1, 12 bits wide
  assign not_1_out = ~r1;  // NOT_Gate not_1, 12 bits wide
  Adder #(.width(12)) adder_1 (.a(r1), .b(r2), .out(adder_1_out));  // open: cin, cout
  Subtractor #(.width(12)) subtractor_1 (.a(r1), .b(r2), .out(subtractor_1_out));  // open: bin, bout
  Shifter #(.width(12)) shifter_1 (.in(r1));  // open: dist, out
  Multiplexer #(.select(3), .width(12)) multiplexer_1 (
    .in0(and_1_out), .in1(or_1_out), .in2(xor_1_out), .in3(not_1_out), .in4(adder_1_out),
    .in5(subtractor_1_out), .out(O), .sel(op));  // open: in6, in7
endmodule
